# Fritzing sketch Clock (saved by Fritzing 0.9.2b)
circuit board: 1.97214cm x 2.13304cm
circuit board: 1.97214cm x 2.13304cm
circuit board: 1.97214cm x 2.13304cm
circuit board: 10cm x 6cm
circuit board: 1.97214cm x 2.13304cm
circuit board: 1.97214cm x 2.13304cm
circuit board: 1.97214cm x 2.13304cm

parts:
  R5 = Resistor [tolerance=±5% resistance=1k package="1206 [SMD]"]
  J6 = female pin header, 7 pins [form="♀ (female)"]
  Part2 = IN-14 nixie tube [part_number=IN-14 package=THT]
  J7 = female pin header, 7 pins [form="♀ (female)"]
  Part3 = IN-14 nixie tube [part_number=IN-14 package=THT]
  IC1 = DS3231MZ Real Time Clock
  U1 = HV5522PG [part_number=HV5522PG package=tqfp44]
  J8 = female pin header, 7 pins [form="♀ (female)"]
  Q1 = NPN-Transistor [package="SOT-23 [SMD]"]
  R3 = Resistor [tolerance=±5% resistance=1k package="1206 [SMD]"]
  J4 = female pin header, 7 pins [form="♀ (female)"]
  Q2 = NPN-Transistor [package="SOT-23 [SMD]"]
  Part6 = IN-14 nixie tube [part_number=IN-14 package=THT]
  J12 = female pin header, 7 pins [form="♀ (female)"]
  J14 = female pin header, 7 pins [form="♀ (female)"]
  J3 = female pin header, 7 pins [form="♀ (female)"]
  Teensy1 = Teensy 2.0
  J11 = female pin header, 7 pins [form="♀ (female)"]
  Q3 = NPN-Transistor [package="SOT-23 [SMD]"]
  R4 = Resistor [tolerance=±5% resistance=10k package="1206 [SMD]"]
  J9 = female pin header, 7 pins [form="♀ (female)"]
  Part7 = IN-14 nixie tube [part_number=IN-14 package=THT]
  Part5 = IN-14 nixie tube [part_number=IN-14 package=THT]
  R2 = Resistor [tolerance=±5% resistance=10k package="1206 [SMD]"]
  J10 = female pin header, 7 pins [form="♀ (female)"]
  U2 = HV5522PG [part_number=HV5522PG package=tqfp44]
  J5 = female pin header, 7 pins [form="♀ (female)"]
  C1 = Capacitor [package=1210]
  Part4 = IN-14 nixie tube [part_number=IN-14 package=THT]
  R1 = Resistor [tolerance=±5% resistance=1k package="1206 [SMD]"]
  R6 = Resistor [tolerance=±5% resistance=10k package="1206 [SMD]"]
  J13 = female pin header, 7 pins [form="♀ (female)"]

nets:
  CLK5: R5.Pin_0, Teensy1.B2
  N1: R5.Pin_1, Q3.0
  N2: J6.pin1, Part3.pin9
  N3: J6.pin2, Part3.pin8
  N4: J6.pin3, Part3.pin7
  N5: J6.pin4, Part3.pin6
  N6: J6.pin5, Part3.pin5
  N7: J6.pin6, Part3.pin4
  N8: J6.pin7, Part3.pin3
  170V: Part2.Anode, Part3.Anode, Part6.Anode, J3.pin4, J11.pin4, J9.pin4, Part7.Anode, Part5.Anode, J5.pin4, J13.pin4
  N9: Part2.pinPL, J3.pin5
  N10: Part2.pin1, J3.pin6
  N11: Part2.pin2, J3.pin7
  N12: Part2.pin3, J4.pin7
  N13: Part2.pin4, J4.pin6
  N14: Part2.pin5, J4.pin5
  N15: Part2.pin6, J4.pin4
  N16: Part2.pin7, J4.pin3
  N17: Part2.pin8, J4.pin2
  N18: Part2.pin9, J4.pin1
  N19: Part2.pin0, J3.pin2
  N20: Part2.pinPR, J3.pin3
  N21: J7.pin2, Part4.pin0
  N22: J7.pin3, Part4.pinPR
  N23: J7.pin4, Part4.Anode
  N24: J7.pin5, Part4.pinPL
  N25: J7.pin6, Part4.pin1
  N26: J7.pin7, Part4.pin2
  N27: Part3.pinPL, J5.pin5
  N28: Part3.pin1, J5.pin6
  N29: Part3.pin2, J5.pin7
  N30: Part3.pin0, J5.pin2
  N31: Part3.pinPR, J5.pin3
  5V: IC1.Pin_2, Teensy1.VCC, C1.1
  GND: IC1.Pin_5, U1.VSS, Q1.2, Q2.2, Teensy1.GND, Q3.2, U2.VSS, C1.2
  SDA: IC1.Pin_7, Teensy1.D1
  SCL: IC1.Pin_8, Teensy1.D0
  N32: U1.DATA_OUT, U2.DATA_IN
  CLK12: U1.CLK, Q3.1, U2.CLK, R6.Pin_0
  12V: U1.VDD, R4.Pin_1, R2.Pin_1, U2.VDD, R6.Pin_1
  LE12: U1.LE, Q2.1, R4.Pin_0, U2.LE
  DATA12: U1.DATA_IN, Q1.1, R2.Pin_0
  N33: J8.pin1, Part4.pin9
  N34: J8.pin2, Part4.pin8
  N35: J8.pin3, Part4.pin7
  N36: J8.pin4, Part4.pin6
  N37: J8.pin5, Part4.pin5
  N38: J8.pin6, Part4.pin4
  N39: J8.pin7, Part4.pin3
  N40: Q1.0, R1.Pin_1
  LE5: R3.Pin_0, Teensy1.B3
  N41: R3.Pin_1, Q2.0
  N42: Part6.pinPL, J11.pin5
  N43: Part6.pin1, J11.pin6
  N44: Part6.pin2, J11.pin7
  N45: Part6.pin3, J12.pin7
  N46: Part6.pin4, J12.pin6
  N47: Part6.pin5, J12.pin5
  N48: Part6.pin6, J12.pin4
  N49: Part6.pin7, J12.pin3
  N50: Part6.pin8, J12.pin2
  N51: Part6.pin9, J12.pin1
  N52: Part6.pin0, J11.pin2
  N53: Part6.pinPR, J11.pin3
  N54: J14.pin1, Part7.pin9
  N55: J14.pin2, Part7.pin8
  N56: J14.pin3, Part7.pin7
  N57: J14.pin4, Part7.pin6
  N58: J14.pin5, Part7.pin5
  N59: J14.pin6, Part7.pin4
  N60: J14.pin7, Part7.pin3
  DATA5: Teensy1.B7, R1.Pin_0
  N61: J9.pin2, Part5.pin0
  N62: J9.pin3, Part5.pinPR
  N63: J9.pin5, Part5.pinPL
  N64: J9.pin6, Part5.pin1
  N65: J9.pin7, Part5.pin2
  N66: Part7.pinPL, J13.pin5
  N67: Part7.pin1, J13.pin6
  N68: Part7.pin2, J13.pin7
  N69: Part7.pin0, J13.pin2
  N70: Part7.pinPR, J13.pin3
  N71: Part5.pin3, J10.pin7
  N72: Part5.pin4, J10.pin6
  N73: Part5.pin5, J10.pin5
  N74: Part5.pin6, J10.pin4
  N75: Part5.pin7, J10.pin3
  N76: Part5.pin8, J10.pin2
  N77: Part5.pin9, J10.pin1

custom parts:
  IN-14 nixie tube: IN-14 nixie tube footprint
  DS3231MZ Real Time Clock: DS3231MZ Real Time Clock. SO-8 surface mount version.
  HV5522PG: High-Voltage Driver Chip (Open-Drain)
