# Fritzing sketch NixiePad (saved by Fritzing 0.9.2b)
breadboards: 1

parts:
  Part2 = IN-14 nixie tube [part_number=IN-14 package=THT]

nets:
  N1: Part2.pinPL, Part2.pin2
  N2: Part2.pin1, Part2.pin9
  N3: Part2.pin3, Part2.pin7
  N4: Part2.pin4, Part2.pin5, Part2.pin6, Part2.pin0, Part2.pinPR

custom parts:
  IN-14 nixie tube: IN-14 nixie tube footprint
