# Fritzing sketch Riser (saved by Fritzing 0.9.2b)
circuit board: 1.97214cm x 2.13304cm
breadboards: 1

parts:
  Part1 = IN-14 nixie tube [part_number=IN-14 package=THT]
  J1 = female pin header, 7 pins [form="♀ (female)"]
  J2 = female pin header, 7 pins [form="♀ (female)"]

nets:
  N1: Part1.Anode, J2.pin4
  N2: Part1.pinPL, J2.pin5
  N3: Part1.pin1, J2.pin6
  N4: Part1.pin2, J2.pin7
  N5: Part1.pin3, J1.pin7
  N6: Part1.pin4, J1.pin6
  N7: Part1.pin5, J1.pin5
  N8: Part1.pin6, J1.pin4
  N9: Part1.pin7, J1.pin3
  N10: Part1.pin8, J1.pin2
  N11: Part1.pin9, J1.pin1
  N12: Part1.pin0, J2.pin2
  N13: Part1.pinPR, J2.pin3

custom parts:
  IN-14 nixie tube: IN-14 nixie tube footprint
